# Fritzing sketch blinkm (saved by Fritzing 0.8.7b)
breadboards: 1

parts:
  R2 = Resistor [tolerance=±5% resistance=4.7k package=THT]
  R3 = Resistor [tolerance=±5% resistance=4.7k package=THT]
  U1 = mystery part, 4 pins [chip_label=BlinkM]

nets:
  N1: R2.Pin_0, R3.Pin_0, U1.pin2
  N2: R2.Pin_1, U1.pin4
  N3: R3.Pin_1, U1.pin3

notes:
  GND
  SDL
  SDA
  +V
