# Fritzing sketch lcd (saved by Fritzing 0.8.7b)
breadboards: 1

parts:
  LCD_I2C1 = LCD screen I2C
  R2 = Resistor [tolerance=±5% resistance=4.7k package=THT]
  R3 = Resistor [tolerance=±5% resistance=4.7k package=THT]

nets:
  N1: LCD_I2C1.VCC, R2.Pin_0, R3.Pin_0
  N2: LCD_I2C1.SDA, R3.Pin_1
  N3: LCD_I2C1.SCL, R2.Pin_1

notes:
  GND
  SDL
  SDA
  +V

custom parts:
  LCD screen I2C: Character display, I2C interface, 2x16 characters.
