# Fritzing sketch analog_sensor (saved by Fritzing 0.8.7b)
breadboards: 1

parts:
  R1 = Resistor [tolerance=±5% resistance=10k package=THT]
  R2 = Photocell (LDR) [package=THT]

nets:
  N1: R1.Pin_1, R2.pin_0

notes:
  GND
  Pin
  +V
