# Fritzing sketch motor (saved by Fritzing 0.8.7b)
breadboards: 1

parts:
  R1 = Resistor [tolerance=±5% resistance=270 package=THT]
  M1 = DC Motor
  Q1 = PNP-Transistor [package="TO92 [THT]"]
  D1 = Rectifier Diode [part_number=1N4001 package="300 mil [THT]"]

nets:
  N1: R1.Pin_0, Q1.B
  N2: M1.pin_1, D1.cathode
  N3: M1.pin_2, Q1.C, D1.anode

notes:
  GND
  Pin
  +V
