# Fritzing sketch hmc6352 (saved by Fritzing 0.8.7b)
breadboards: 1

parts:
  R2 = Resistor [tolerance=±5% resistance=4.7k package=THT]
  R3 = Resistor [tolerance=±5% resistance=4.7k package=THT]
  U2 = HMC6352 [package=lcc24]

nets:
  N1: R2.Pin_0, R3.Pin_0, U2.VCC
  N2: R2.Pin_1, U2.SCL
  N3: R3.Pin_1, U2.SDA

notes:
  GND
  SDL
  SDA
  +V
