# Fritzing sketch mpl115a2 (saved by Fritzing 0.8.7b)
breadboards: 1

parts:
  R2 = Resistor [tolerance=±5% resistance=4.7k package=THT]
  R3 = Resistor [tolerance=±5% resistance=4.7k package=THT]
  SENSOR1 = MPL115A2 Barometer Breakout Board

nets:
  N1: R2.Pin_0, R3.Pin_0, SENSOR1.VDD
  N2: R2.Pin_1, SENSOR1.SCL
  N3: R3.Pin_1, SENSOR1.SDA

notes:
  GND
  SDL
  SDA
  +V

custom parts:
  MPL115A2 Barometer Breakout Board: MPL115A2 I2C Barometric Sensor
